// Logisim project ALU.circ as structural Verilog: 8 circuits, main circuit OR
module OR (
  input  [3:0] A,
  input  [3:0] B,
  output [3:0] O
);

  _7432 u_7432_1 (
    ._1__1A(A[3]), ._2__1B(B[3]), ._3__1Y(O[3]), ._4__2A(A[2]), ._5__2B(B[2]), ._6__2Y(O[2]), ._13__4B(A[1]),
    ._12__4A(B[1]), ._11__4Y(O[1]), ._10__3B(A[0]), ._9__3A(B[0]), ._8__3Y(O[0]));  // open: _7__GND, _14__Vcc
endmodule

module AND (
  input  [3:0] A,
  input  [3:0] B,
  output [3:0] O
);

  _7408 u_7408_1 (
    ._1__1A(A[3]), ._2__1B(B[3]), ._3__1Y(O[3]), ._4__2A(A[2]), ._5__2B(B[2]), ._6__2Y(O[2]), ._13__4B(A[1]),
    ._12__4A(B[1]), ._11__4Y(O[1]), ._10__3B(A[0]), ._9__3A(B[0]), ._8__3Y(O[0]));  // open: _7__GND, _14__Vcc
endmodule

module NOR (
  input  [3:0] A,
  input  [3:0] B,
  output [3:0] O
);

  _7402 u_7402_1 (
    ._1__1Y(O[3]), ._2__1A(A[3]), ._3__1B(B[3]), ._4__2Y(O[2]), ._5__2A(A[2]), ._6__2B(B[2]), ._13__4Y(O[1]),
    ._12__4B(A[1]), ._11__4A(B[1]), ._10__3Y(O[0]), ._9__3B(A[0]), ._8__3A(B[0]));  // open: _7__GND, _14__Vcc
endmodule

module ADD (
  input  [3:0] A,
  input  [3:0] B,
  output [3:0] O
);

  Adder #(.width(4)) adder_1 (.a(A), .b(B), .out(O), .cin(1'b0));  // open: cout
endmodule

module SUB (
  input  [3:0] A,
  input  [3:0] B,
  output [3:0] O
);

  Subtractor #(.width(4)) subtractor_1 (.a(A), .b(B), .out(O), .bin(1'b0));  // open: bout
endmodule

module SRL (
  input  [3:0] A,
  input  [3:0] Shamt,
  output [3:0] O
);

  wire n7432_1__3__1y;
  wire [3:0] shifter_1_out;

  Shifter #(.width(4), .shift("lr")) shifter_1 (.in(A), .\dist (Shamt[1:0]), .out(shifter_1_out));
  _7432 u_7432_1 (
    ._1__1A(Shamt[2]), ._2__1B(Shamt[3]), ._3__1Y(n7432_1__3__1y));  // open: _4__2A, _5__2B, _6__2Y, _7__GND, _14__Vcc, _13__4B, _12__4A, _11__4Y, _10__3B, _9__3A, _8__3Y
  _4Mux2X1 u_4mux2x1_1 (.E_prime(1'b0), .A(shifter_1_out), .B(4'b0000), .S(n7432_1__3__1y), .O(O));
endmodule

module SLL (
  input  [3:0] A,
  input  [3:0] Shamt,
  output [3:0] O
);

  wire n7432_1__3__1y;
  wire [3:0] shifter_1_out;

  Shifter #(.width(4)) shifter_1 (.in(A), .\dist (Shamt[1:0]), .out(shifter_1_out));
  _7432 u_7432_1 (
    ._1__1A(Shamt[2]), ._2__1B(Shamt[3]), ._3__1Y(n7432_1__3__1y));  // open: _4__2A, _5__2B, _6__2Y, _7__GND, _14__Vcc, _13__4B, _12__4A, _11__4Y, _10__3B, _9__3A, _8__3Y
  _4Mux2X1 u_4mux2x1_1 (.E_prime(1'b0), .A(shifter_1_out), .B(4'b0000), .S(n7432_1__3__1y), .O(O));
endmodule

module ALU (
  input  [3:0] A,
  input  [3:0] B,
  input  [2:0] ALUOP,
  output [3:0] _4
);

  wire [3:0] add_1_o, and_1_o, nor_1_o, or_1_o, sll_1_o, srl_1_o, sub_1_o;

  ADD add_1 (.A(A), .B(B), .O(add_1_o));
  SUB sub_1 (.A(A), .B(B), .O(sub_1_o));
  OR or_1 (.A(A), .B(B), .O(or_1_o));
  AND and_1 (.A(A), .B(B), .O(and_1_o));
  SLL sll_1 (.A(A), .Shamt(B), .O(sll_1_o));
  SRL srl_1 (.A(A), .Shamt(B), .O(srl_1_o));
  NOR nor_1 (.A(A), .B(B), .O(nor_1_o));
  Multiplexer #(.select(3), .width(4)) multiplexer_1 (
    .in0(add_1_o), .in1(sub_1_o), .in2(or_1_o), .in3(and_1_o), .in4(sll_1_o), .in5(srl_1_o), .in6(nor_1_o),
    .out(_4), .sel(ALUOP), .en(1'b1));  // open: in7
endmodule
