// Logisim project ControlLib.circ as structural Verilog: 1 circuit, main circuit Control
// Ctrl
module Control (
  input  [15:0] Ins,
  output [2:0] AluOP,
  output Jump,
  output rWrite,
  output mWrite,
  output A_M,
  output R_I,
  output Dest,
  output JR,
  output Cjump
);

  ROM #(.addrWidth(6), .dataWidth(11), .Select("low")) rom_1 (
    .addr({Ins[15:14], Ins[3:0]}), .data({Cjump, JR, Dest, R_I, A_M, mWrite, rWrite, Jump, AluOP}), .sel(1'b0));

  // Notes on the sheet:
  //   contents of rom_1 (hex, n*v repeats v):
  //   16 195 13 194 480 88 193 191 1d0 a0 11 190 12 480 192 10 5*0 288 15*0 80
endmodule
