// Logisim project ID.circ as structural Verilog: 3 circuits, main circuit register bank
// Register Bank
module register_bank (
  input  write,
  input  [3:0] write_address,
  input  [7:0] write_data,
  input  [3:0] rs,
  input  [3:0] rt,
  input  clk,
  input  clk_2,
  input  clk_4,
  output [3:0] out_9,
  output [7:0] data1,
  output [7:0] data2
);

  wire and_1_out, not_1_out, not_2_out, not_3_out;
  wire [3:0] multiplexer_2_out;

  and and_1 (and_1_out, write, clk, clk_2);
  not not_1 (not_1_out, clk_4);
  Multiplexer #(.width(4), .enable("false")) multiplexer_1 (
    .in0(rs), .in1(write_address), .out(out_9), .sel(and_1_out));
  not not_2 (not_2_out, and_1_out);
  Multiplexer #(.width(4), .enable("false")) multiplexer_2 (
    .in0(rt), .in1(write_address), .out(multiplexer_2_out), .sel(and_1_out));
  RAM #(.addrWidth(4), .Select("low")) ram_1 (
    .addr(out_9), .data(data1), .sel(1'b0), .clk(not_1_out), .ld(not_2_out));  // open: clr
  not not_3 (not_3_out, not_2_out);
  RAM #(.addrWidth(4), .Select("low")) ram_2 (
    .addr(multiplexer_2_out), .data(data2), .sel(1'b0), .clk(not_1_out), .ld(not_2_out));  // open: clr
  assign data1 = not_3_out ? write_data : 8'bz;  // Controlled_Buffer controlled_buffer_1
  assign data2 = not_3_out ? write_data : 8'bz;  // Controlled_Buffer controlled_buffer_2
endmodule

module ID (
  input  [3:0] segment,
  input  write,
  input  [3:0] write_address,
  input  [7:0] write_data,
  input  [15:0] instruction,
  input  clk,
  input  clk_2,
  input  clk_4,
  input  cjmp,
  input  regdest,
  input  rjmp,
  output [3:0] jmp_segment,
  output [7:0] data1,
  output [7:0] data2,
  output [7:0] jmp_pc,
  output [3:0] jmp_offset,
  output [3:0] writereg,
  output [3:0] imd
);

  wire and_1_out, comparator_1_eq, xor_1_out;

  register_bank register_bank_1 (
    .rs(instruction[7:4]), .rt(instruction[11:8]), .data1(data1), .data2(data2), .write(write),
    .write_address(write_address), .write_data(write_data), .clk(clk), .clk_2(clk_2), .clk_4(clk_4));  // open: out_9
  Comparator comparator_1 (.a(data2), .b(data1), .eq(comparator_1_eq));  // open: gt, lt
  xor xor_1 (xor_1_out, comparator_1_eq, instruction[3]);
  and and_1 (and_1_out, xor_1_out, cjmp);
  Multiplexer #(.width(4), .enable("false")) multiplexer_1 (
    .in0(segment), .in1(data2[3:0]), .out(jmp_segment), .sel(rjmp));
  Multiplexer #(.width(8), .enable("false")) multiplexer_2 (
    .in0(instruction[11:4]), .in1(data1), .out(jmp_pc), .sel(rjmp));
  Multiplexer #(.width(4), .enable("false")) multiplexer_3 (
    .in0(4'b0000), .in1(instruction[15:12]), .out(jmp_offset), .sel(and_1_out));
  Multiplexer #(.width(4), .enable("false")) multiplexer_4 (
    .in0(instruction[15:12]), .in1(instruction[11:8]), .out(writereg), .sel(regdest));

  assign imd = instruction[15:12];
endmodule

// Clock Generator
module clock_generator (
  output clk_4,
  output clk_2,
  output clk
);

  Clock clock_1 (.out(clk_4));
  T_Flip_Flop t_ff_1 (.clk(clk_4), .T(clk_4), .Q(clk_2));  // open: Qn, preset, reset
  T_Flip_Flop t_ff_2 (.clk(clk_2), .T(clk_2), .Q(clk));  // open: Qn, preset, reset
endmodule
