// Logisim project MIPS.circ as structural Verilog: 1 circuit, main circuit main
module main (
  input  in_1,
  input  in_2
);

  wire clock_generator_1_clk, clock_generator_1_clk_2, clock_generator_1_clk_4, controldecoder_1_jump,
       controldecoder_2_a_m, controldecoder_2_mwrite, controldecoder_2_r_i, controldecoder_3_a_m,
       controldecoder_3_mwrite, id_1_p3, id_1_p5, id_1_p9, id_1_p10, id_1_p12, or_1_out;
  wire [2:0] controldecoder_2_aluop;
  wire [3:0] id_1_p8, id_1_p13, id_1_p17, id_1_p18, id_1_p19, instructionfetch_1_segment, pr_1_out_10,
       pr_2_out_10, pr_2_out_11, pr_3_out_10;
  wire [7:0] execution_1_ans, id_1_p11, id_1_p14, id_1_p15, id_1_p16, mem_1_val, pr_2_out_8, pr_2_out_9,
       pr_3_out_8, pr_3_out_9;
  wire [10:0] control_1_control, pr_2_out_13, pr_3_out_13, pr_4_out_13;
  wire [15:0] instructionfetch_1_instruction, pr_1_out_12;

  clock_generator clock_generator_1 (
    .clk_4(clock_generator_1_clk_4), .clk_2(clock_generator_1_clk_2), .clk(clock_generator_1_clk));
  InstructionFetch instructionfetch_1 (
    .PrevSeg(id_1_p13), .Offset(id_1_p17), .SegClr(in_1), .PCClear(in_2), .UJumpAddress(id_1_p16),
    .Instruction(instructionfetch_1_instruction), .UJump(controldecoder_1_jump), .NoOp(or_1_out),
    .clk(clock_generator_1_clk), .segment(instructionfetch_1_segment));  // open: SegPreset, PCPreset
  or or_1 (or_1_out, id_1_p3, controldecoder_1_jump);
  pr pr_1 (
    .in_3(instructionfetch_1_segment), .in_5(instructionfetch_1_instruction), .out_10(pr_1_out_10),
    .out_12(pr_1_out_12), .clk(clock_generator_1_clk));  // open: in_1, in_2, in_4, in_6, out_8, out_9, out_11, out_13
  // ID id_1: pin names not known; wires that end beside it: pr_1_out_10, pr_1_out_12, id_1_p3, clock_generator_1_clk, id_1_p5, clock_generator_1_clk_2, clock_generator_1_clk_4, id_1_p8, id_1_p9, id_1_p10, id_1_p11, id_1_p12, id_1_p13, id_1_p14, id_1_p15, id_1_p16, id_1_p17, id_1_p18, id_1_p19
  Control control_1 (.Ins(pr_1_out_12), .control(control_1_control));
  ControlDecoder controldecoder_1 (
    .in_1(control_1_control), .Jump(controldecoder_1_jump), .Dest(id_1_p10), .JR(id_1_p12), .Cjump(id_1_p9));  // open: AluOP, rWrite, mWrite, A_M, R_I
  pr pr_2 (
    .in_1(id_1_p14), .in_2(id_1_p15), .in_3(id_1_p19), .in_4(id_1_p18), .in_6(control_1_control),
    .out_8(pr_2_out_8), .out_9(pr_2_out_9), .out_10(pr_2_out_10), .out_11(pr_2_out_11), .out_13(pr_2_out_13),
    .clk(clock_generator_1_clk));  // open: in_5, out_12
  ControlDecoder controldecoder_2 (
    .in_1(pr_2_out_13), .AluOP(controldecoder_2_aluop), .mWrite(controldecoder_2_mwrite),
    .A_M(controldecoder_2_a_m), .R_I(controldecoder_2_r_i));  // open: Jump, rWrite, Dest, JR, Cjump
  Execution execution_1 (
    .Data1(pr_2_out_8), .Data2(pr_2_out_9), .Imd(pr_2_out_10), .Ans(execution_1_ans),
    .mWrite(controldecoder_2_mwrite), .mRead(controldecoder_2_a_m), .R_I(controldecoder_2_r_i),
    .AluOp(controldecoder_2_aluop));
  pr pr_3 (
    .in_1(execution_1_ans), .in_2(pr_2_out_9), .in_3(pr_2_out_11), .in_6(pr_2_out_13), .out_8(pr_3_out_8),
    .out_9(pr_3_out_9), .out_10(pr_3_out_10), .out_13(pr_3_out_13), .clk(clock_generator_1_clk));  // open: in_4, in_5, out_11, out_12
  ControlDecoder controldecoder_3 (
    .in_1(pr_3_out_13), .mWrite(controldecoder_3_mwrite), .A_M(controldecoder_3_a_m));  // open: AluOP, Jump, rWrite, R_I, Dest, JR, Cjump
  mem mem_1 (
    .Address__res(pr_3_out_8), .WriteData__Data1(pr_3_out_9), .memWrite(controldecoder_3_mwrite),
    .nRAMEnable(1'b0), .val(mem_1_val), .memRead(controldecoder_3_a_m), .clk(clock_generator_1_clk));  // open: ReadData, Clear
  pr pr_4 (
    .in_1(mem_1_val), .in_3(pr_3_out_10), .in_6(pr_3_out_13), .out_8(id_1_p11), .out_10(id_1_p8),
    .out_13(pr_4_out_13), .clk(clock_generator_1_clk));  // open: in_2, in_4, in_5, out_9, out_11, out_12
  ControlDecoder controldecoder_4 (
    .in_1(pr_4_out_13), .rWrite(id_1_p5));  // open: AluOP, Jump, mWrite, A_M, R_I, Dest, JR, Cjump
endmodule
