// Logisim project Memory.circ as structural Verilog: 1 circuit, main circuit mem
// Mem
module mem (
  input  memRead,
  input  [7:0] Address__res,
  input  [7:0] WriteData__Data1,
  input  memWrite,
  input  clk,
  input  nRAMEnable,
  input  Clear,
  output [7:0] val,
  output [7:0] ReadData
);

  RAM #(.bus("separate"), .simpleMode("false"), .Select("low")) ram_1 (
    .addr(Address__res), .din(WriteData__Data1), .data(ReadData), .str(memWrite), .sel(nRAMEnable),
    .clk(clk), .clr(Clear));  // open: ld
  _8Mux2X1 u_8mux2x1_1 (.E_prime(1'b0), .A(Address__res), .B(ReadData), .S(memRead), .out_5(val));
endmodule
